# Fritzing sketch cs_05_23 (saved by Fritzing 0.9.2b)
breadboards: 1

parts:
  Часть1 = Arduino Uno (Rev3)
  VCC1 = Battery block 9V  # not connected
  Часть2 = Arduino Motor Shield (Rev3)
  M2 = DC Motor
  L1 = Inductor [package="400 mil [THT]"]
  R1 = Photocell (LDR) [package=THT]
  LED1 = LED - 5mm [color="Red (633nm)" package="5 mm [THT]"]  # not connected
  M1 = DC Motor
  J1 = Basic Servo
  R2 = Resistor [tolerance=±5% resistance=10k package=THT]
  R4 = Trimmer Potentiometer [maximum_resistance=10kΩ package=THT]

nets:
  N1: Часть1.A0, R1.pin_0, R4.wiper
  N2: Часть1.D3_PWM, L1.pin_0
  N3: Часть1.5V, R1.pin_1, R2.Pin_0, R4.leg1
  N4: Часть1.GND, L1.pin_1, R4.leg2
  N5: Часть2.B-, M1.pin_2
  N6: Часть2.B+, M1.pin_1
  N7: Часть2.A-, M2.pin_2
  N8: Часть2.A+, M2.pin_1
  GND: Часть2.GND, J1.gnd
  N9: Часть2.D6_PWM, J1.vcc
  N10: Часть2.5V, J1.pulse
